// Logisim project cputest.circ as structural Verilog: 7 circuits, main circuit main
module main (
  input  in_1,
  input  in_2,
  input  in_3,
  output [4:0] out_4
);

  wire Clock, clock_2_out, clock_3_out, comparator_1_lt, counter_1_carry, multiplexer_1_out, not_1_out,
       Reset, TClock;
  wire [2:0] A, B, D, rom_1_data;
  wire [3:0] multiplexer_2_out, OpCode;
  wire [4:0] counter_1_q, MSB;
  wire [6:0] adder_1_out, decoder_1_out0, LSB;
  wire [8:0] Data, R0, R1, R2, R3, R4, R5, R6;

  Multiplexer multiplexer_1 (.in0(in_1), .in1(in_2), .out(multiplexer_1_out), .sel(in_3));  // open: en
  Clock clock_1 (.out(Clock));
  LED led_1 (.in(multiplexer_1_out));
  Program_Counter program_counter_1 (.clock(Clock), .\output (out_4));
  RAM #(.addrWidth(5), .dataWidth(22)) ram_1 (
    .addr(out_4), .data({OpCode, A, B, D, Data}), .clk(Clock), .clr(Reset));  // open: sel, ld
  Decoder #(.select(3)) decoder_1 (
    .out0(decoder_1_out0[0]), .out1(decoder_1_out0[1]), .out2(decoder_1_out0[2]), .out3(decoder_1_out0[3]),
    .out4(decoder_1_out0[4]), .out5(decoder_1_out0[5]), .out6(decoder_1_out0[6]), .sel(D));  // open: out7, en
  // Probe on D
  // Probe on decoder_1_out0
  Register_Bank register_bank_1 (
    .in_3(clock_2_out), .in_2(decoder_1_out0));  // open: in_1, Register_Outputs, out_5, out_6, out_7, out_8, out_9, out_10
  Clock clock_2 (.out(clock_2_out));
  TTY #(.rows(33), .cols(1)) tty_1 (.data(LSB), .clk(TClock), .clr(Reset));  // open: we
  TTY #(.rows(33), .cols(1)) tty_2 (.data({2'b10, MSB}), .clk(TClock), .clr(Reset));  // open: we
  Button u_Reset (.out(Reset));
  Counter #(.width(5), .max('h1f), .ongoal("stay")) counter_1 (
    .Q(counter_1_q), .carry(counter_1_carry), .clk(TClock), .clr(Reset));  // open: load, D, count
  Multiplexer #(.select(3), .width(9), .disabled(0), .enable("false")) multiplexer_2 (
    .in0(R0), .in1(R1), .in2(R2), .in3(R3), .in4(R4), .in5(R5), .in6(R6), .out({MSB, multiplexer_2_out}),
    .sel(rom_1_data));  // open: in7
  not not_1 (not_1_out, counter_1_carry);
  Clock clock_3 (.out(clock_3_out));
  ROM #(.addrWidth(5), .dataWidth(3)) rom_1 (.addr(counter_1_q), .data(rom_1_data));  // open: sel
  and and_1 (TClock, not_1_out, clock_3_out);
  // Probe on {3'b011, multiplexer_2_out}
  // Probe on {2'b10, MSB}
  Comparator #(.width(7)) comparator_1 (
    .a(7'b0111001), .b({3'b011, multiplexer_2_out}), .lt(comparator_1_lt));  // open: gt, eq
  Adder #(.width(7)) adder_1 (.a({3'b011, multiplexer_2_out}), .b(7'b0000111), .out(adder_1_out));  // open: cin, cout
  // Probe on LSB
  Multiplexer #(.width(7), .disabled(0), .enable("false")) multiplexer_3 (
    .in0({3'b011, multiplexer_2_out}), .in1(adder_1_out), .out(LSB), .sel(comparator_1_lt));

  // Notes on the sheet:
  //   Donna Chow
  //   determines which operation to perform
  //   Destination register
  //   @0
  //   JA
  //   E5
  //   @0
  //   OF
  //   U5
  //   OF
  //   E5
  //   E5
  //   U4
  //   E5
  //   E5
  //   U4
  //   _F
  //   _F
  //   _F
  //   AF
  //   AF
  //   AF
  //   @0
  //   AE
  //   AE
  //   AE
  //   _E
  //   OF
  //   ^0
  //   J9
  //   P1
  //   R0
  //   R0
  //   _F
  //   contents of rom_1 (hex, n*v repeats v):
  //   0 0 1 2 3 4 5 6 6 2 3 4 5 6 6 0 1 2 3 4 5 6 6 2 3 4 5 6 6 6
endmodule

module ALU (
  input  [8:0] Register_A,
  input  [8:0] Register_B,
  input  in_3
);

  wire C8, n3_bit_adder_1_out_18, n3_bit_adder_1_out_19, n3_bit_adder_1_out_20, n3_bit_adder_1_out_21,
       n3_bit_adder_1_out_22, n3_bit_adder_1_out_23, n3_bit_adder_2_out_18, n3_bit_adder_2_out_19,
       n3_bit_adder_2_out_20, n3_bit_adder_2_out_21, n3_bit_adder_2_out_22, n3_bit_adder_2_out_23,
       n3_bit_adder_3_out_18, n3_bit_adder_3_out_19, n3_bit_adder_3_out_20, n3_bit_adder_3_out_21,
       n3_bit_adder_3_out_22, n3_bit_adder_3_out_23, n9_bit_carry_look_ahead_1_out_22,
       n9_bit_carry_look_ahead_1_out_23, n9_bit_carry_look_ahead_1_out_24, n9_bit_carry_look_ahead_1_out_27,
       n9_bit_carry_look_ahead_1_out_28, n9_bit_carry_look_ahead_1_out_29, nA0, nA1, nA2, nA3, nA4, nA5, nA6,
       nA7, nA8;

  _9_Bit_Carry_Look_Ahead u_9_bit_carry_look_ahead_1 (
    .in_3(n3_bit_adder_3_out_19), .in_4(n3_bit_adder_3_out_20), .in_5(n3_bit_adder_3_out_21),
    .in_6(n3_bit_adder_3_out_22), .in_7(n3_bit_adder_3_out_23), .out_22(n9_bit_carry_look_ahead_1_out_22),
    .out_23(n9_bit_carry_look_ahead_1_out_23), .out_24(n9_bit_carry_look_ahead_1_out_24),
    .in_8(n9_bit_carry_look_ahead_1_out_24), .in_9(n3_bit_adder_2_out_18), .in_10(n3_bit_adder_2_out_19),
    .in_11(n3_bit_adder_2_out_20), .in_12(n3_bit_adder_2_out_21), .in_13(n3_bit_adder_2_out_22),
    .out_27(n9_bit_carry_look_ahead_1_out_27), .in_14(n3_bit_adder_2_out_23),
    .in_15(n9_bit_carry_look_ahead_1_out_27), .in_16(n3_bit_adder_1_out_18),
    .out_28(n9_bit_carry_look_ahead_1_out_28), .in_17(n3_bit_adder_1_out_19), .in_18(n3_bit_adder_1_out_20),
    .out_29(n9_bit_carry_look_ahead_1_out_29), .in_19(n3_bit_adder_1_out_21), .in_20(n3_bit_adder_1_out_22),
    .out_30(C8), .in_21(n3_bit_adder_1_out_23), .in_2(n3_bit_adder_3_out_18));  // open: in_1, out_25, out_26
  _3_Bit_Adder u_3_bit_adder_1 (
    .in_1(Register_A[6]), .in_2(Register_B[6]), .in_3(Register_A[7]), .in_4(Register_B[7]),
    .in_5(Register_A[8]), .in_6(Register_B[8]), .in_9(n9_bit_carry_look_ahead_1_out_27),
    .in_10(n9_bit_carry_look_ahead_1_out_28), .in_11(n9_bit_carry_look_ahead_1_out_29),
    .out_18(n3_bit_adder_1_out_18), .out_19(n3_bit_adder_1_out_19), .out_20(n3_bit_adder_1_out_20),
    .out_21(n3_bit_adder_1_out_21), .out_22(n3_bit_adder_1_out_22), .out_23(n3_bit_adder_1_out_23));  // open: in_7, in_8, out_12, out_13, out_14, out_15, out_16, out_17
  _3_Bit_Adder u_3_bit_adder_2 (
    .in_1(Register_A[3]), .in_2(Register_B[3]), .in_3(Register_A[4]), .in_4(Register_B[4]),
    .in_5(Register_A[5]), .in_6(Register_B[5]), .in_9(n9_bit_carry_look_ahead_1_out_24),
    .out_18(n3_bit_adder_2_out_18), .out_19(n3_bit_adder_2_out_19), .out_20(n3_bit_adder_2_out_20),
    .out_21(n3_bit_adder_2_out_21), .out_22(n3_bit_adder_2_out_22), .out_23(n3_bit_adder_2_out_23));  // open: in_7, in_8, in_10, in_11, out_12, out_13, out_14, out_15, out_16, out_17
  not not_1 (nA0, Register_A[0]);
  not not_2 (nA1, Register_A[1]);
  not not_3 (nA2, Register_A[2]);
  not not_4 (nA3, Register_A[3]);
  not not_5 (nA4, Register_A[4]);
  not not_6 (nA5, Register_A[5]);
  not not_7 (nA6, Register_A[6]);
  not not_8 (nA7, Register_A[7]);
  not not_9 (nA8, Register_A[8]);
  // Probe on in_3
  _3_Bit_Adder u_3_bit_adder_3 (
    .in_1(Register_A[0]), .in_2(Register_B[0]), .in_3(Register_A[1]), .in_4(Register_B[1]),
    .in_5(Register_A[2]), .in_6(Register_B[2]), .in_10(n9_bit_carry_look_ahead_1_out_22),
    .in_11(n9_bit_carry_look_ahead_1_out_23), .out_18(n3_bit_adder_3_out_18), .out_19(n3_bit_adder_3_out_19),
    .out_20(n3_bit_adder_3_out_20), .out_21(n3_bit_adder_3_out_21), .out_22(n3_bit_adder_3_out_22),
    .out_23(n3_bit_adder_3_out_23));  // open: in_7, in_8, in_9, out_12, out_13, out_14, out_15, out_16, out_17

  // Other names for the same wires on the sheet: OpCode = in_3; A0 = Register_A[0]; A1 = Register_A[1];
  //   A2 = Register_A[2]; A3 = Register_A[3]; A4 = Register_A[4]; A5 = Register_A[5]; A6 = Register_A[6];
  //   A7 = Register_A[7]; A8 = Register_A[8]; B0 = Register_B[0]; B1 = Register_B[1]; B2 = Register_B[2];
  //   B3 = Register_B[3]; B4 = Register_B[4]; B5 = Register_B[5]; B6 = Register_B[6]; B7 = Register_B[7];
  //   B8 = Register_B[8]

  // Notes on the sheet:
  //   Input:
  //   P = OR
  //   Need to split bits so we can do operations on them
  //   G = AND
  //   Addition
  //   NOT A
  //   Actual carries
  //   sums
endmodule

module Register_Bank (
  input  [8:0] in_1,
  input  [6:0] in_2,
  input  in_3,
  output [8:0] Register_Outputs,
  output [8:0] out_5,
  output [8:0] out_6,
  output [8:0] out_7,
  output [8:0] out_8,
  output [8:0] out_9,
  output [8:0] out_10
);

  wire [8:0] multiplexer_1_out, multiplexer_2_out, multiplexer_3_out, multiplexer_4_out, multiplexer_5_out,
       multiplexer_6_out, multiplexer_7_out;

  Multiplexer #(.width(9)) multiplexer_1 (
    .in0(Register_Outputs), .in1(in_1), .out(multiplexer_1_out), .sel(in_2[0]));  // open: en
  Multiplexer #(.width(9)) multiplexer_2 (.in0(out_5), .in1(in_1), .out(multiplexer_2_out), .sel(in_2[1]));  // open: en
  Multiplexer #(.width(9)) multiplexer_3 (.in0(out_6), .in1(in_1), .out(multiplexer_3_out), .sel(in_2[2]));  // open: en
  Multiplexer #(.width(9)) multiplexer_4 (.in0(out_7), .in1(in_1), .out(multiplexer_4_out), .sel(in_2[3]));  // open: en
  Multiplexer #(.width(9)) multiplexer_5 (.in0(out_8), .in1(in_1), .out(multiplexer_5_out), .sel(in_2[4]));  // open: en
  Multiplexer #(.width(9)) multiplexer_6 (.in0(out_9), .in1(in_1), .out(multiplexer_6_out), .sel(in_2[5]));  // open: en
  Multiplexer #(.width(9)) multiplexer_7 (
    .in0(out_10), .in1(in_1), .out(multiplexer_7_out), .sel(in_2[6]));  // open: en
  D_Flip_Flop d_ff_1 (.clk(in_3), .D(multiplexer_2_out[0]), .Q(out_5[0]));  // open: Qn, preset, en, reset
  D_Flip_Flop d_ff_2 (.clk(in_3), .D(multiplexer_3_out[0]), .Q(out_6[0]));  // open: Qn, preset, en, reset
  D_Flip_Flop d_ff_3 (.clk(in_3), .D(multiplexer_1_out[1]), .Q(Register_Outputs[1]));  // open: Qn, preset, en, reset
  D_Flip_Flop d_ff_4 (.clk(in_3), .D(multiplexer_1_out[0]), .Q(Register_Outputs[0]));  // open: Qn, preset, en, reset
  D_Flip_Flop d_ff_5 (.clk(in_3), .D(multiplexer_2_out[1]), .Q(out_5[1]));  // open: Qn, preset, en, reset
  D_Flip_Flop d_ff_6 (.clk(in_3), .D(multiplexer_3_out[1]), .Q(out_6[1]));  // open: Qn, preset, en, reset
  D_Flip_Flop d_ff_7 (.clk(in_3), .D(multiplexer_4_out[0]), .Q(out_7[0]));  // open: Qn, preset, en, reset
  D_Flip_Flop d_ff_8 (.clk(in_3), .D(multiplexer_5_out[0]), .Q(out_8[0]));  // open: Qn, preset, en, reset
  D_Flip_Flop d_ff_9 (.clk(in_3), .D(multiplexer_6_out[0]), .Q(out_9[0]));  // open: Qn, preset, en, reset
  D_Flip_Flop d_ff_10 (.clk(in_3), .D(multiplexer_7_out[0]), .Q(out_10[0]));  // open: Qn, preset, en, reset
  D_Flip_Flop d_ff_11 (.clk(in_3), .D(multiplexer_1_out[2]), .Q(Register_Outputs[2]));  // open: Qn, preset, en, reset
  D_Flip_Flop d_ff_12 (.clk(in_3), .D(multiplexer_2_out[2]), .Q(out_5[2]));  // open: Qn, preset, en, reset
  D_Flip_Flop d_ff_13 (.clk(in_3), .D(multiplexer_3_out[2]), .Q(out_6[2]));  // open: Qn, preset, en, reset
  D_Flip_Flop d_ff_14 (.clk(in_3), .D(multiplexer_4_out[1]), .Q(out_7[1]));  // open: Qn, preset, en, reset
  D_Flip_Flop d_ff_15 (.clk(in_3), .D(multiplexer_5_out[1]), .Q(out_8[1]));  // open: Qn, preset, en, reset
  D_Flip_Flop d_ff_16 (.clk(in_3), .D(multiplexer_6_out[1]), .Q(out_9[1]));  // open: Qn, preset, en, reset
  D_Flip_Flop d_ff_17 (.clk(in_3), .D(multiplexer_6_out[2]), .Q(out_9[2]));  // open: Qn, preset, en, reset
  D_Flip_Flop d_ff_18 (.clk(in_3), .D(multiplexer_7_out[1]), .Q(out_10[1]));  // open: Qn, preset, en, reset
  D_Flip_Flop d_ff_19 (.clk(in_3), .D(multiplexer_1_out[3]), .Q(Register_Outputs[3]));  // open: Qn, preset, en, reset
  D_Flip_Flop d_ff_20 (.clk(in_3), .D(multiplexer_2_out[3]), .Q(out_5[3]));  // open: Qn, preset, en, reset
  D_Flip_Flop d_ff_21 (.clk(in_3), .D(multiplexer_3_out[3]), .Q(out_6[3]));  // open: Qn, preset, en, reset
  D_Flip_Flop d_ff_22 (.clk(in_3), .D(multiplexer_4_out[3]), .Q(out_7[3]));  // open: Qn, preset, en, reset
  D_Flip_Flop d_ff_23 (.clk(in_3), .D(multiplexer_4_out[2]), .Q(out_7[2]));  // open: Qn, preset, en, reset
  D_Flip_Flop d_ff_24 (.clk(in_3), .D(multiplexer_5_out[3]), .Q(out_8[3]));  // open: Qn, preset, en, reset
  D_Flip_Flop d_ff_25 (.clk(in_3), .D(multiplexer_5_out[2]), .Q(out_8[2]));  // open: Qn, preset, en, reset
  D_Flip_Flop d_ff_26 (.clk(in_3), .D(multiplexer_6_out[3]), .Q(out_9[3]));  // open: Qn, preset, en, reset
  D_Flip_Flop d_ff_27 (.clk(in_3), .D(multiplexer_7_out[3]), .Q(out_10[3]));  // open: Qn, preset, en, reset
  D_Flip_Flop d_ff_28 (.clk(in_3), .D(multiplexer_7_out[2]), .Q(out_10[2]));  // open: Qn, preset, en, reset
  D_Flip_Flop d_ff_29 (.clk(in_3), .D(multiplexer_1_out[4]), .Q(Register_Outputs[4]));  // open: Qn, preset, en, reset
  D_Flip_Flop d_ff_30 (.clk(in_3), .D(multiplexer_2_out[4]), .Q(out_5[4]));  // open: Qn, preset, en, reset
  D_Flip_Flop d_ff_31 (.clk(in_3), .D(multiplexer_3_out[4]), .Q(out_6[4]));  // open: Qn, preset, en, reset
  D_Flip_Flop d_ff_32 (.clk(in_3), .D(multiplexer_4_out[4]), .Q(out_7[4]));  // open: Qn, preset, en, reset
  D_Flip_Flop d_ff_33 (.clk(in_3), .D(multiplexer_5_out[4]), .Q(out_8[4]));  // open: Qn, preset, en, reset
  D_Flip_Flop d_ff_34 (.clk(in_3), .D(multiplexer_6_out[4]), .Q(out_9[4]));  // open: Qn, preset, en, reset
  D_Flip_Flop d_ff_35 (.clk(in_3), .D(multiplexer_7_out[4]), .Q(out_10[4]));  // open: Qn, preset, en, reset
  D_Flip_Flop d_ff_36 (.clk(in_3), .D(multiplexer_1_out[5]), .Q(Register_Outputs[5]));  // open: Qn, preset, en, reset
  D_Flip_Flop d_ff_37 (.clk(in_3), .D(multiplexer_2_out[5]), .Q(out_5[5]));  // open: Qn, preset, en, reset
  D_Flip_Flop d_ff_38 (.clk(in_3), .D(multiplexer_3_out[5]), .Q(out_6[5]));  // open: Qn, preset, en, reset
  D_Flip_Flop d_ff_39 (.clk(in_3), .D(multiplexer_4_out[5]), .Q(out_7[5]));  // open: Qn, preset, en, reset
  D_Flip_Flop d_ff_40 (.clk(in_3), .D(multiplexer_5_out[5]), .Q(out_8[5]));  // open: Qn, preset, en, reset
  D_Flip_Flop d_ff_41 (.clk(in_3), .D(multiplexer_6_out[5]), .Q(out_9[5]));  // open: Qn, preset, en, reset
  D_Flip_Flop d_ff_42 (.clk(in_3), .D(multiplexer_7_out[5]), .Q(out_10[5]));  // open: Qn, preset, en, reset
  D_Flip_Flop d_ff_43 (.clk(in_3), .D(multiplexer_1_out[6]), .Q(Register_Outputs[6]));  // open: Qn, preset, en, reset
  D_Flip_Flop d_ff_44 (.clk(in_3), .D(multiplexer_2_out[6]), .Q(out_5[6]));  // open: Qn, preset, en, reset
  D_Flip_Flop d_ff_45 (.clk(in_3), .D(multiplexer_3_out[6]), .Q(out_6[6]));  // open: Qn, preset, en, reset
  D_Flip_Flop d_ff_46 (.clk(in_3), .D(multiplexer_4_out[6]), .Q(out_7[6]));  // open: Qn, preset, en, reset
  D_Flip_Flop d_ff_47 (.clk(in_3), .D(multiplexer_5_out[6]), .Q(out_8[6]));  // open: Qn, preset, en, reset
  D_Flip_Flop d_ff_48 (.clk(in_3), .D(multiplexer_6_out[6]), .Q(out_9[6]));  // open: Qn, preset, en, reset
  D_Flip_Flop d_ff_49 (.clk(in_3), .D(multiplexer_7_out[6]), .Q(out_10[6]));  // open: Qn, preset, en, reset
  D_Flip_Flop d_ff_50 (.clk(in_3), .D(multiplexer_1_out[7]), .Q(Register_Outputs[7]));  // open: Qn, preset, en, reset
  D_Flip_Flop d_ff_51 (.clk(in_3), .D(multiplexer_2_out[8]), .Q(out_5[8]));  // open: Qn, preset, en, reset
  D_Flip_Flop d_ff_52 (.clk(in_3), .D(multiplexer_2_out[7]), .Q(out_5[7]));  // open: Qn, preset, en, reset
  D_Flip_Flop d_ff_53 (.clk(in_3), .D(multiplexer_3_out[7]), .Q(out_6[7]));  // open: Qn, preset, en, reset
  D_Flip_Flop d_ff_54 (.clk(in_3), .D(multiplexer_3_out[8]), .Q(out_6[8]));  // open: Qn, preset, en, reset
  D_Flip_Flop d_ff_55 (.clk(in_3), .D(multiplexer_4_out[7]), .Q(out_7[7]));  // open: Qn, preset, en, reset
  D_Flip_Flop d_ff_56 (.clk(in_3), .D(multiplexer_5_out[7]), .Q(out_8[7]));  // open: Qn, preset, en, reset
  D_Flip_Flop d_ff_57 (.clk(in_3), .D(multiplexer_6_out[7]), .Q(out_9[7]));  // open: Qn, preset, en, reset
  D_Flip_Flop d_ff_58 (.clk(in_3), .D(multiplexer_7_out[7]), .Q(out_10[7]));  // open: Qn, preset, en, reset
  D_Flip_Flop d_ff_59 (.clk(in_3), .D(multiplexer_1_out[8]), .Q(Register_Outputs[8]));  // open: Qn, preset, en, reset
  D_Flip_Flop d_ff_60 (.clk(in_3), .D(multiplexer_4_out[8]), .Q(out_7[8]));  // open: Qn, preset, en, reset
  D_Flip_Flop d_ff_61 (.clk(in_3), .D(multiplexer_5_out[8]), .Q(out_8[8]));  // open: Qn, preset, en, reset
  D_Flip_Flop d_ff_62 (.clk(in_3), .D(multiplexer_6_out[8]), .Q(out_9[8]));  // open: Qn, preset, en, reset
  D_Flip_Flop d_ff_63 (.clk(in_3), .D(multiplexer_7_out[8]), .Q(out_10[8]));  // open: Qn, preset, en, reset

  // Other names for the same wires on the sheet: Clock = in_3; DataIn[8:0] = in_1; R0 = in_2[0]; R1 = in_2[1];
  //   R2 = in_2[2]; R3 = in_2[3]; R4 = in_2[4]; R5 = in_2[5]; R6 = in_2[6]; O0[8:0] = Register_Outputs;
  //   O1[8:0] = out_5; O2[8:0] = out_6; O3[8:0] = out_7; O4[8:0] = out_8; O5[8:0] = out_9; O6[8:0] = out_10

  // Notes on the sheet:
  //   9 bits we're writing into a register, coming from ALU
  //   LSB
  //   LSB
  //   LSB
  //   LSB
  //   LSB
  //   LSB
  //   LSB
  //   When one of these =1, it will write the data into the register, else it'll just write it's original output
  //   Determine Desgination Register (From Decoder) (write Enabled -)>only bit is 'high'
  //   MSB
  //   MSB
  //   MSB
  //   MSB
  //   MSB
  //   MSB
  //   MSB
  //   Register 0
  //   Register 1
  //   Register 2
  //   Register 5
  //   Register 3
  //   Register 4
  //   Register 6
endmodule

module _9_Bit_Carry_Look_Ahead (
  input  in_1,
  input  in_2,
  input  in_3,
  input  in_4,
  input  in_5,
  input  in_6,
  input  in_7,
  input  in_8,
  input  in_9,
  input  in_10,
  input  in_11,
  input  in_12,
  input  in_13,
  input  in_14,
  input  in_15,
  input  in_16,
  input  in_17,
  input  in_18,
  input  in_19,
  input  in_20,
  input  in_21,
  output out_22,
  output out_23,
  output out_24,
  output out_25,
  output out_26,
  output out_27,
  output out_28,
  output out_29,
  output out_30
);

  wire and_1_out, and_2_out, and_3_out, cinp0p1p2_2_out, cinp0p1p2_3_out, cinp0p1p2_out, g0p1p2_2_out,
       g0p1p2_3_out, g0p1p2_out, g1p2_2_out, g1p2_3_out, g1p2_out, p0_c0_2_out, p0_c0_3_out, p0_c0_out,
       p1_g0_2_out, p1_g0_3_out, p1_g0_out;

  and p0_c0 (p0_c0_out, in_1, in_2);
  and p1_g0 (p1_g0_out, in_3, in_4);
  and and_1 (and_1_out, in_1, in_2, in_4);
  and g1p2 (g1p2_out, in_5, in_6);
  and g0p1p2 (g0p1p2_out, in_3, in_4, in_6);
  and cinp0p1p2 (cinp0p1p2_out, in_1, in_2, in_4);
  and p0_c0_2 (p0_c0_2_out, in_8, in_9);
  and p1_g0_2 (p1_g0_2_out, in_10, in_11);
  and and_2 (and_2_out, in_8, in_9, in_11);
  and g1p2_2 (g1p2_2_out, in_12, in_13);
  and g0p1p2_2 (g0p1p2_2_out, in_10, in_11, in_13);
  and cinp0p1p2_2 (cinp0p1p2_2_out, in_8, in_9, in_11);
  and p0_c0_3 (p0_c0_3_out, in_15, in_16);
  and p1_g0_3 (p1_g0_3_out, in_17, in_18);
  and and_3 (and_3_out, in_15, in_16, in_18);
  and g1p2_3 (g1p2_3_out, in_19, in_20);
  and g0p1p2_3 (g0p1p2_3_out, in_17, in_18, in_20);
  and cinp0p1p2_3 (cinp0p1p2_3_out, in_15, in_16, in_18);
  or g0_plus (out_22, p0_c0_out, in_3);
  or g1_plus (out_23, p1_g0_out, and_1_out, in_5);
  or plus_g2 (out_24, g1p2_out, g0p1p2_out, cinp0p1p2_out, in_7);
  or g0_plus_2 (out_25, p0_c0_2_out, in_10);
  or g1_plus_2 (out_26, p1_g0_2_out, and_2_out, in_12);
  or plus_g2_2 (out_27, g1p2_2_out, g0p1p2_2_out, cinp0p1p2_2_out, in_14);
  or g0_plus_3 (out_28, p0_c0_3_out, in_17);
  or g1_plus_3 (out_29, p1_g0_3_out, and_3_out, in_19);
  or plus_g2_3 (out_30, g1p2_3_out, g0p1p2_3_out, cinp0p1p2_3_out, in_21);

  // Notes on the sheet:
  //   Carry Look Ahead (generating carries)
  //   cin*p0*p1
  //   cin*p0*p1
  //   cin*p0*p1
endmodule

module _3_Bit_Adder (
  input  in_1,
  input  in_2,
  input  in_3,
  input  in_4,
  input  in_5,
  input  in_6,
  input  in_7,
  input  in_8,
  input  in_9,
  input  in_10,
  input  in_11,
  output out_12,
  output out_13,
  output out_14,
  output out_15,
  output out_16,
  output out_17,
  output out_18,
  output out_19,
  output out_20,
  output out_21,
  output out_22,
  output out_23
);

  wire not_1_out, not_2_out, not_3_out, xor_1_out, xor_2_out, xor_3_out;

  not not_1 (not_1_out, in_1);
  xor xor_1 (xor_1_out, in_1, in_2);
  not not_2 (not_2_out, in_3);
  not not_3 (not_3_out, in_5);
  xor carryin (out_15, xor_1_out, in_9);
  xor xor_2 (xor_2_out, in_3, in_4);
  xor carryin_2 (out_16, xor_2_out, in_10);
  xor xor_3 (xor_3_out, in_5, in_6);
  xor carryin_3 (out_17, xor_3_out, in_11);
  Multiplexer #(.select(2)) multiplexer_1 (
    .in0(out_19), .in1(out_18), .in2(not_1_out), .in3(out_15), .out(out_12), .sel({in_8, in_7}));  // open: en
  Multiplexer #(.select(2)) multiplexer_2 (
    .in0(out_21), .in1(out_20), .in2(not_2_out), .in3(out_16), .out(out_13), .sel({in_8, in_7}));  // open: en
  Multiplexer #(.select(2)) multiplexer_3 (
    .in0(out_23), .in1(out_22), .in2(not_3_out), .in3(out_17), .out(out_14), .sel({in_8, in_7}));  // open: en
  and and_1 (out_19, in_1, in_2);
  or or_1 (out_18, in_2, in_1);
  and and_2 (out_21, in_3, in_4);
  or or_2 (out_20, in_4, in_3);
  and and_3 (out_23, in_5, in_6);
  or or_3 (out_22, in_6, in_5);

  // Other names for the same wires on the sheet: sb0 = in_7; sb1 = in_8; A0 = in_1; A1 = in_3; A2 = in_5; B0 = in_2;
  //   B1 = in_4; B2 = in_6; C0 = out_12; C1 = out_13; C2 = out_14; C_1 = in_10; C_2 = in_11; CIN = in_9; G0 = out_19;
  //   G1 = out_21; G2 = out_23; P0 = out_18; P1 = out_20; P2 = out_22; S0 = out_15; S1 = out_16; S2 = out_17

  // Notes on the sheet:
  //   G = AND
  //   adder...
  //   adder...
  //   adder...
  //   NOT A
  //   P = OR
  //   G = AND
  //   Generating P/G
  //   P = OR
endmodule

module Program_Counter (
  input  clock,
  output [4:0] \output 
);

  wire d_ff_1_qn, d_ff_2_qn, d_ff_3_qn, d_ff_4_qn, d_ff_5_qn;

  D_Flip_Flop d_ff_1 (.clk(clock), .D(d_ff_1_qn), .Q(\output [0]), .Qn(d_ff_1_qn));  // open: preset, en, reset
  D_Flip_Flop d_ff_2 (.clk(d_ff_1_qn), .D(d_ff_2_qn), .Q(\output [1]), .Qn(d_ff_2_qn));  // open: preset, en, reset
  D_Flip_Flop d_ff_3 (.clk(d_ff_2_qn), .D(d_ff_3_qn), .Q(\output [2]), .Qn(d_ff_3_qn));  // open: preset, en, reset
  D_Flip_Flop d_ff_4 (.clk(d_ff_3_qn), .D(d_ff_4_qn), .Q(\output [3]), .Qn(d_ff_4_qn));  // open: preset, en, reset
  D_Flip_Flop d_ff_5 (.clk(d_ff_4_qn), .D(d_ff_5_qn), .Q(\output [4]), .Qn(d_ff_5_qn));  // open: preset, en, reset

  // Notes on the sheet:
  //   LSB
  //   MSB
endmodule

module _9_bit_Register (
  input  [8:0] in_1,
  input  in_2,
  input  in_3,
  output [8:0] out_4
);

  wire [8:0] multiplexer_1_out;

  Multiplexer #(.width(9)) multiplexer_1 (.in0(out_4), .in1(in_1), .out(multiplexer_1_out), .sel(in_2));  // open: en
  D_Flip_Flop d_ff_1 (.clk(in_3), .D(multiplexer_1_out[0]), .Q(out_4[0]));  // open: Qn, preset, en, reset
  D_Flip_Flop d_ff_2 (.clk(in_3), .D(multiplexer_1_out[1]), .Q(out_4[1]));  // open: Qn, preset, en, reset
  D_Flip_Flop d_ff_3 (.clk(in_3), .D(multiplexer_1_out[2]), .Q(out_4[2]));  // open: Qn, preset, en, reset
  D_Flip_Flop d_ff_4 (.clk(in_3), .D(multiplexer_1_out[3]), .Q(out_4[3]));  // open: Qn, preset, en, reset
  D_Flip_Flop d_ff_5 (.clk(in_3), .D(multiplexer_1_out[4]), .Q(out_4[4]));  // open: Qn, preset, en, reset
  D_Flip_Flop d_ff_6 (.clk(in_3), .D(multiplexer_1_out[5]), .Q(out_4[5]));  // open: Qn, preset, en, reset
  D_Flip_Flop d_ff_7 (.clk(in_3), .D(multiplexer_1_out[6]), .Q(out_4[6]));  // open: Qn, preset, en, reset
  D_Flip_Flop d_ff_8 (.clk(in_3), .D(multiplexer_1_out[7]), .Q(out_4[7]));  // open: Qn, preset, en, reset
  D_Flip_Flop d_ff_9 (.clk(in_3), .D(multiplexer_1_out[8]), .Q(out_4[8]));  // open: Qn, preset, en, reset

  // Other names for the same wires on the sheet: Clock = in_3; DataIn[8:0] = in_1; Output[8:0] = out_4;
  //   Register_Selection = in_2

  // Notes on the sheet:
  //   LSB
  //   MSB
  //   Register 5
endmodule
